# Fritzing sketch viverino (saved by Fritzing 0.9.3b)
breadboards: 1

parts:
  Part1 = Arduino Uno (Rev3)
  DS1 = DS18B20 1-Wire Temperature Sensor [part_number=DS18B20]
  RHT1 = Humidity and Temperature Sensor RHT03
  R1 = Photocell (LDR) [package=THT]
  Part2 = Soil Moisture Sensor
  L1 = Solenoid
  WeMos_D1_Mini_Relay_Shield_V1 = WeMos D1 Mini Relay Shield V2
  R2 = Resistor [tolerance=±5% resistance=10k package="2512 [SMD]"]
  R3 = Resistor [tolerance=±5% resistance=4.7 package=THT]
  R4 = Resistor [tolerance=±5% resistance=10k package="2512 [SMD]"]

nets:
  N1: Part1.A0, R2.Pin_1
  N2: Part1.A1, R3.Pin_1
  N3: Part1.A2, Part2.SIG
  GND: Part1.GND, RHT1.GND_2, Part2.GND, WeMos_D1_Mini_Relay_Shield_V1.G, R2.Pin_0
  3V3: Part1.AREF, Part1.3V3, DS1.VDD, R1.pin_0, R3.Pin_0
  N4: Part1.D2, R4.Pin_0
  5V: Part1.5V, Part2.VCC, WeMos_D1_Mini_Relay_Shield_V1.5V, R4.Pin_1
  N5: L1.pin2, WeMos_D1_Mini_Relay_Shield_V1.NO

notes:
  alimentacao de 110V
  Sistema de ativacao da agua
